# Fritzing sketch DeLaSalle (saved by Fritzing 0.9.4)
breadboards: 1

parts:
  L298N1 = L298N DC motor driver
  M1 = Getriebemotor
  HC-SR04_Sensor_1 = HC-SR04 Ultrasonic Distance Sensor
  M2 = Getriebemotor
  Part1 = Arduino Uno (Rev3) - ICSP

nets:
  N1: L298N1.OUT1, M2.pin_2
  N2: L298N1.OUT2, M2.pin_1
  N3: L298N1.OUT3, M1.pin_2
  N4: L298N1.OUT4, M1.pin_1
  GND: L298N1.GND, HC-SR04_Sensor_1.GND, Part1.GND
  VCC: L298N1.5V#7, HC-SR04_Sensor_1.VCC, Part1.5V
  N5: L298N1.5V#9, L298N1.ENA
  N6: L298N1.5V#10, L298N1.ENB
  N7: L298N1.IN1, Part1.D2
  N8: L298N1.IN2, Part1.D3_PWM
  N9: L298N1.IN3, Part1.D4
  N10: L298N1.IN4, Part1.D5_PWM
  N11: HC-SR04_Sensor_1.TRIG, Part1.ICSP_MISO, Part1.D12/MISO
  N12: HC-SR04_Sensor_1.ECHO, Part1.D11_PWM/MOSI

custom parts:
  L298N DC motor driver: 2x DC motor driver with 78M05 positive voltage regulator (7..35 V) L298N: max 46 V, 2 A Set 5 V Enable jumper to enable 5 V regultor (needed for the L298N) and +5 V output at screw terminal or supply external +5 V at screw terminal Set ENA and/or ENB to +5 V to enable motor permanently or supply ENA and/or ENB with PWM signal IN1 and IN2 set rotation directory for motor A (OUT1/OUT2) IN2 and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
