# Fritzing sketch amazing race (saved by Fritzing 0.9.6b)
breadboards: 1

parts:
  R1 = Resistor [tolerance=±5% power=0.25 resistance=220 package=THT]
  R2 = Resistor [tolerance=±5% power=0.25 resistance=220 package=THT]
  R3 = Resistor [tolerance=±5% power=0.25 resistance=220 package=THT]
  LED1 = LED - 3mm [color="Red (633nm)" current=0.030 package="3 mm [THT]"]
  LED2 = LED - 3mm [color="Yellow (592nm)" current=0.030 package="3 mm [THT]"]
  LED3 = LED - 3mm [color="Green (565nm)" current=0.030 package="3 mm [THT]"]
  HC-SR04_Sensor_1 = HC-SR04 Ultrasonic Distance Sensor
  Part1 = Arduino Uno (Rev3) - ICSP

nets:
  N1: R1.Pin_0, LED1.cathode
  GND: R1.Pin_1, R2.Pin_1, R3.Pin_1, HC-SR04_Sensor_1.GND, Part1.GND
  N2: R2.Pin_0, LED2.cathode
  N3: R3.Pin_0, LED3.cathode
  N4: LED1.anode, Part1.D4
  N5: LED2.anode, Part1.D3_PWM
  N6: LED3.anode, Part1.D2
  VCC: HC-SR04_Sensor_1.VCC, Part1.5V
  N7: HC-SR04_Sensor_1.TRIG, Part1.D9_PWM
  N8: HC-SR04_Sensor_1.ECHO, Part1.D10_PWM/SS
